// Logisim project Calculadora P1.circ as structural Verilog: 10 circuits, main circuit main
module main (
  input  in_1,
  input  in_2,
  input  in_3,
  input  in_4,
  input  in_5,
  input  in_6,
  input  in_7,
  input  in_8,
  input  in_9,
  input  in_10,
  input  in_11,
  input  in_12,
  input  in_13,
  input  in_14,
  input  in_15,
  input  in_16,
  output A_B,
  output A_B_2,
  output A_B_3
);

  wire [3:0] CALCULADORA_out_11, DECODER_2_out_11, DECODER_out_11;

  Hex_Digit_Display hex_digit_display_1 (.value(DECODER_out_11));  // open: dp
  Hex_Digit_Display hex_digit_display_2 (.value(DECODER_2_out_11));  // open: dp
  decodificador_inverso DECODER (
    .out_9(DECODER_out_11[2]), .out_10(DECODER_out_11[1]), .out_11(DECODER_out_11[0]),
    .out_8(DECODER_out_11[3]), .a(in_1), .b(in_3), .c(in_6), .d(in_7), .e(in_5), .f(in_2), .g(in_4));
  decodificador_inverso DECODER_2 (
    .out_9(DECODER_2_out_11[2]), .out_10(DECODER_2_out_11[1]), .out_11(DECODER_2_out_11[0]),
    .out_8(DECODER_2_out_11[3]), .a(in_8), .b(in_10), .c(in_13), .d(in_14), .e(in_12), .f(in_9), .g(in_11));
  calculadora CALCULADORA (
    .a0(DECODER_out_11[0]), .a1(DECODER_out_11[1]), .a2(DECODER_out_11[2]), .a3(DECODER_out_11[3]),
    .b0(DECODER_2_out_11[0]), .b1(DECODER_2_out_11[1]), .b2(DECODER_2_out_11[2]), .b3(DECODER_2_out_11[3]),
    .in_9(in_15), .in_10(in_16), .out_11(CALCULADORA_out_11[0]), .out_12(CALCULADORA_out_11[1]),
    .out_13(CALCULADORA_out_11[2]), .out_14(CALCULADORA_out_11[3]));
  // Comparador_de_magnitude COMPARADOR: pin names not known; wires that end beside it: DECODER_out_11[3], DECODER_2_out_11[3], DECODER_out_11[2], DECODER_2_out_11[2], DECODER_out_11[1], DECODER_2_out_11[1], DECODER_out_11[0], DECODER_2_out_11[0], A_B, A_B_2, A_B_3
  Hex_Digit_Display hex_digit_display_3 (.value(CALCULADORA_out_11));  // open: dp
endmodule

module Decodificador (
  input  a,
  input  b,
  input  c,
  input  d,
  output out_5,
  output out_6,
  output out_7,
  output out_8,
  output out_9,
  output out_10,
  output out_11
);

  wire and_1_out, and_2_out, and_3_out, and_4_out, and_5_out, and_6_out, and_7_out, and_8_out, and_9_out,
       and_10_out, and_11_out, and_12_out, and_13_out, and_14_out, and_15_out, and_16_out, and_17_out,
       and_18_out, and_19_out, and_20_out, and_21_out, and_22_out, and_23_out, and_24_out, and_25_out,
       and_26_out, and_27_out, and_28_out, and_29_out, and_30_out, and_31_out, and_32_out, and_33_out,
       and_34_out, and_35_out, and_36_out, not_1_out, not_2_out, not_3_out, not_4_out, not_5_out, not_6_out,
       not_7_out, not_8_out, not_9_out, not_10_out, not_11_out, not_12_out, not_13_out, not_14_out,
       not_15_out, not_16_out, not_17_out, not_18_out, not_19_out, not_20_out, not_21_out, not_22_out,
       not_23_out, not_24_out, not_25_out, not_26_out, not_27_out, not_28_out, not_29_out, not_30_out,
       not_31_out, not_32_out, not_33_out, not_34_out, not_35_out, not_36_out, not_37_out, not_38_out,
       not_39_out, not_40_out, not_41_out, not_42_out, not_43_out, not_44_out, or_1_out, or_2_out, or_3_out,
       or_4_out;

  not not_1 (not_1_out, a);
  not not_2 (not_2_out, d);
  not not_3 (not_3_out, b);
  not not_4 (not_4_out, d);
  not not_5 (not_5_out, a);
  not not_6 (not_6_out, b);
  not not_7 (not_7_out, c);
  not not_8 (not_8_out, b);
  not not_9 (not_9_out, c);
  not not_10 (not_10_out, b);
  not not_11 (not_11_out, d);
  not not_12 (not_12_out, a);
  not not_13 (not_13_out, c);
  not not_14 (not_14_out, d);
  not not_15 (not_15_out, a);
  not not_16 (not_16_out, c);
  not not_17 (not_17_out, a);
  not not_18 (not_18_out, b);
  not not_19 (not_19_out, c);
  not not_20 (not_20_out, a);
  not not_21 (not_21_out, c);
  not not_22 (not_22_out, a);
  not not_23 (not_23_out, c);
  not not_24 (not_24_out, d);
  not not_25 (not_25_out, b);
  not not_26 (not_26_out, a);
  not not_27 (not_27_out, b);
  not not_28 (not_28_out, d);
  not not_29 (not_29_out, c);
  not not_30 (not_30_out, d);
  not not_31 (not_31_out, d);
  not not_32 (not_32_out, b);
  not not_33 (not_33_out, d);
  not not_34 (not_34_out, b);
  not not_35 (not_35_out, d);
  not not_36 (not_36_out, c);
  not not_37 (not_37_out, d);
  not not_38 (not_38_out, a);
  not not_39 (not_39_out, c);
  not not_40 (not_40_out, b);
  not not_41 (not_41_out, b);
  not not_42 (not_42_out, d);
  not not_43 (not_43_out, a);
  not not_44 (not_44_out, c);
  and and_1 (and_1_out, not_1_out, c);
  and and_2 (and_2_out, b, c);
  and and_3 (and_3_out, not_2_out, a);
  and and_4 (and_4_out, not_3_out, not_4_out);
  and and_5 (and_5_out, d, b, not_5_out);
  and and_6 (and_6_out, a, not_6_out, not_7_out);
  and and_7 (and_7_out, not_8_out, not_9_out);
  and and_8 (and_8_out, not_10_out, not_11_out);
  and and_9 (and_9_out, not_12_out, not_13_out, not_14_out);
  and and_10 (and_10_out, not_15_out, c, d);
  and and_11 (and_11_out, a, not_16_out, d);
  and and_12 (and_12_out, not_17_out, b);
  and and_13 (and_13_out, not_18_out, a);
  and and_14 (and_14_out, d, not_19_out);
  and and_15 (and_15_out, not_20_out, not_21_out);
  and and_16 (and_16_out, not_22_out, d);
  and and_17 (and_17_out, a, not_23_out);
  and and_18 (and_18_out, b, c, not_24_out);
  and and_19 (and_19_out, not_25_out, c, d);
  and and_20 (and_20_out, not_26_out, not_27_out, not_28_out);
  and and_21 (and_21_out, b, not_29_out, d);
  and and_22 (and_22_out, a, b);
  and and_23 (and_23_out, c, not_30_out);
  and and_24 (and_24_out, a, c);
  and and_25 (and_25_out, a, not_31_out);
  and and_26 (and_26_out, not_32_out, not_33_out);
  and and_27 (and_27_out, a, not_34_out);
  and and_28 (and_28_out, b, not_35_out);
  and and_29 (and_29_out, not_36_out, not_37_out);
  and and_30 (and_30_out, not_38_out, b, not_39_out);
  and and_31 (and_31_out, a, c);
  and and_32 (and_32_out, not_40_out, c);
  and and_33 (and_33_out, a, not_41_out);
  and and_34 (and_34_out, c, not_42_out);
  and and_35 (and_35_out, a, d);
  and and_36 (and_36_out, not_43_out, b, not_44_out);
  or or_1 (or_1_out, and_1_out, and_2_out, and_3_out, and_4_out);
  or or_2 (or_2_out, and_7_out, and_8_out, and_9_out);
  or or_3 (or_3_out, and_10_out, and_11_out);
  or or_4 (or_4_out, and_5_out, and_6_out);
  _7_Segment_Display u_7_segment_display_1 (
    .g(out_11), .f(out_10), .a(out_5), .b(out_6), .e(out_7), .d(out_8), .c(out_9));  // open: dp
  or or_5 (out_5, or_1_out, or_4_out);
  or or_6 (out_6, or_2_out, or_3_out);
  or or_7 (out_9, and_16_out, and_12_out, and_15_out, and_13_out, and_14_out);
  or or_8 (out_8, and_17_out, and_18_out, and_19_out, and_20_out, and_21_out);
  or or_9 (out_7, and_22_out, and_23_out, and_24_out, and_25_out, and_26_out);
  or or_10 (out_10, and_27_out, and_28_out, and_29_out, and_30_out, and_31_out);
  or or_11 (out_11, and_32_out, and_33_out, and_34_out, and_35_out, and_36_out);
endmodule

module somador (
  input  in_1,
  input  in_2,
  output out_3,
  output out_4
);

  xor xor_1 (out_3, in_1, in_2);
  and and_1 (out_4, in_1, in_2);
endmodule

module fulladder (
  input  ci,
  input  a,
  input  b,
  output out_4,
  output out_5
);

  wire somador_1_out_3, somador_1_out_4, somador_2_out_4;

  somador somador_1 (.in_1(a), .in_2(b), .out_3(somador_1_out_3), .out_4(somador_1_out_4));
  somador somador_2 (.in_1(ci), .in_2(somador_1_out_3), .out_3(out_4), .out_4(somador_2_out_4));
  or or_1 (out_5, somador_2_out_4, somador_1_out_4);
endmodule

module decodificador_inverso (
  input  a,
  input  b,
  input  c,
  input  d,
  input  e,
  input  f,
  input  g,
  output out_8,
  output out_9,
  output out_10,
  output out_11
);

  wire a0_out, a1_out, a1a0_out, a2_out, a2a0_out, a2a1_out, a2a1a0_out, a3_out, a3a0_out, a3a1_out,
       a3a1a0_out, a3a2_out, a3a2a0_out, a3a2a1_out, a3a2a1a0_out;

  _7_Segment_Display u_7_segment_display_1 (.g(g), .f(f), .a(a), .b(b), .e(e), .d(d), .c(c));  // open: dp
  and a0 (a0_out, ~a, b, c, ~d, ~e, ~f, ~g);  // AND_Gate
  and a1 (a1_out, a, b, ~c, d, e, ~f, g);  // AND_Gate
  and a1a0 (a1a0_out, a, b, c, d, ~e, ~f, g);  // AND_Gate
  and a2 (a2_out, ~a, b, c, ~d, ~e, f, g);  // AND_Gate
  and a2a0 (a2a0_out, a, ~b, c, d, ~e, f, g);  // AND_Gate
  and a2a1 (a2a1_out, a, ~b, c, d, e, f, g);  // AND_Gate
  and a2a1a0 (a2a1a0_out, a, b, c, ~d, ~e, ~f, ~g);  // AND_Gate
  and a3 (a3_out, a, b, c, d, e, f, g);
  and a3a0 (a3a0_out, a, b, c, ~d, ~e, f, g);  // AND_Gate
  and a3a1 (a3a1_out, a, b, c, ~d, e, f, g);  // AND_Gate
  and a3a1a0 (a3a1a0_out, ~a, ~b, c, d, e, f, g);  // AND_Gate
  and a3a2 (a3a2_out, a, ~b, ~c, d, e, f, ~g);  // AND_Gate
  and a3a2a0 (a3a2a0_out, ~a, b, c, d, e, ~f, g);  // AND_Gate
  and a3a2a1 (a3a2a1_out, a, ~b, ~c, d, e, f, g);  // AND_Gate
  and a3a2a1a0 (a3a2a1a0_out, a, ~b, ~c, ~d, e, f, g);  // AND_Gate
  or a3_2 (out_8, a3a2a1a0_out, a3a2a1_out, a3a2a0_out, a3a2_out, a3a1a0_out, a3a1_out, a3a0_out, a3_out);
  or a2_2 (out_9, a2_out, a2a0_out, a2a1_out, a2a1a0_out, a3a2_out, a3a2a0_out, a3a2a1_out, a3a2a1a0_out);
  or a1_2 (out_10, a3a1a0_out, a3a2a1_out, a3a2a1a0_out, a3a1_out, a2a1a0_out, a2a1_out, a1_out, a1a0_out);
  or a0_2 (out_11, a0_out, a1a0_out, a2a0_out, a2a1a0_out, a3a0_out, a3a1a0_out, a3a2a0_out, a3a2a1a0_out);

  // Notes on the sheet:
  //   b
  //   a
  //   d
  //   c
  //   e
  //   f
  //   g
endmodule

module multiplicador (
  input  a3,
  input  b3,
  input  a2,
  input  b2,
  input  a1,
  input  b1,
  input  a0,
  input  b0,
  output c7,
  output c6,
  output c5,
  output c4,
  output c3,
  output c2,
  output c1,
  output c0
);

  wire a0b1_out, a0b2_out, a0b3_out, a1b0_out, a1b1_out, a1b2_out, a1b3_out, a2b0_out, a2b1_out, a2b2_out,
       a2b3_out, a3b0_out, a3b1_out, a3b2_out, a3b3_out, fulladder_2_out_4, fulladder_2_out_5,
       fulladder_3_out_5, fulladder_4_out_4, fulladder_4_out_5, fulladder_5_out_4, fulladder_5_out_5,
       fulladder_6_out_4, fulladder_6_out_5, fulladder_7_out_4, fulladder_7_out_5, fulladder_8_out_4,
       fulladder_8_out_5, halfadder_1_out_4, halfadder_2_out_4, halfadder_3_out_4, halfadder_4_out_4;

  and a3b3 (a3b3_out, b3, a3);
  and a3b2 (a3b2_out, b2, a3);
  and a3b1 (a3b1_out, a3, b1);
  and a3b0 (a3b0_out, b0, a3);
  fulladder fulladder_1 (.ci(fulladder_3_out_5), .a(fulladder_2_out_5), .b(a3b3_out), .out_4(c6), .out_5(c7));
  and a2b3 (a2b3_out, b3, a2);
  and a2b2 (a2b2_out, b2, a2);
  fulladder fulladder_2 (
    .ci(fulladder_4_out_5), .a(a2b3_out), .b(a3b2_out), .out_4(fulladder_2_out_4), .out_5(fulladder_2_out_5));
  fulladder fulladder_3 (
    .ci(fulladder_5_out_5), .a(fulladder_2_out_4), .b(halfadder_1_out_4), .out_4(c5),
    .out_5(fulladder_3_out_5));
  and a2b1 (a2b1_out, b1, a2);
  and a2b0 (a2b0_out, b0, a2);
  fulladder fulladder_4 (
    .ci(fulladder_6_out_5), .a(a1b3_out), .b(a2b2_out), .out_4(fulladder_4_out_4), .out_5(fulladder_4_out_5));
  fulladder fulladder_5 (
    .ci(fulladder_7_out_5), .a(fulladder_4_out_4), .b(a3b1_out), .out_4(fulladder_5_out_4),
    .out_5(fulladder_5_out_5));
  halfadder halfadder_1 (.in_1(halfadder_2_out_4), .in_2(fulladder_5_out_4), .out_3(c4), .out_4(halfadder_1_out_4));
  and a1b3 (a1b3_out, b3, a1);
  and a1b2 (a1b2_out, b2, a1);
  and a1b1 (a1b1_out, b1, a1);
  fulladder fulladder_6 (
    .ci(fulladder_8_out_5), .a(a0b3_out), .b(a1b2_out), .out_4(fulladder_6_out_4), .out_5(fulladder_6_out_5));
  fulladder fulladder_7 (
    .ci(halfadder_3_out_4), .a(fulladder_6_out_4), .b(a2b1_out), .out_4(fulladder_7_out_4),
    .out_5(fulladder_7_out_5));
  halfadder halfadder_2 (.in_1(fulladder_7_out_4), .in_2(a3b0_out), .out_3(c3), .out_4(halfadder_2_out_4));
  and a1b0 (a1b0_out, b0, a1);
  and a0b3 (a0b3_out, b3, a0);
  fulladder fulladder_8 (
    .ci(halfadder_4_out_4), .a(a0b2_out), .b(a1b1_out), .out_4(fulladder_8_out_4), .out_5(fulladder_8_out_5));
  halfadder halfadder_3 (.in_1(fulladder_8_out_4), .in_2(a2b0_out), .out_3(c2), .out_4(halfadder_3_out_4));
  and a0b2 (a0b2_out, b2, a0);
  halfadder halfadder_4 (.in_1(a0b1_out), .in_2(a1b0_out), .out_3(c1), .out_4(halfadder_4_out_4));
  and a0b1 (a0b1_out, b1, a0);
  and a0b0 (c0, b0, a0);

  // Notes on the sheet:
  //   a3
  //   b3
  //   a2
  //   b2
  //   a1
  //   b1
  //   a0
  //   b0
endmodule

module halfadder (
  input  in_1,
  input  in_2,
  output out_3,
  output out_4
);

  xor xor_1 (out_3, in_1, in_2);
  and and_1 (out_4, in_1, in_2);
endmodule

module subtrador (
  input  a0,
  input  b0,
  input  a1,
  input  b1,
  input  a2,
  input  b2,
  input  a3,
  input  b3,
  output out_9,
  output out_10,
  output out_11,
  output out_12,
  output out_13
);

  wire fulladder_1_out_5, fulladder_2_out_5, fulladder_3_out_5, xor_1_out, xor_2_out, xor_3_out, xor_4_out;

  xor xor_1 (xor_1_out, b0, 1'b1);
  xor xor_2 (xor_2_out, b1, 1'b1);
  xor xor_3 (xor_3_out, b2, 1'b1);
  xor xor_4 (xor_4_out, b3, 1'b1);
  fulladder fulladder_1 (.ci(1'b1), .a(a0), .b(xor_1_out), .out_4(out_9), .out_5(fulladder_1_out_5));
  fulladder fulladder_2 (.ci(fulladder_1_out_5), .a(a1), .b(xor_2_out), .out_4(out_10), .out_5(fulladder_2_out_5));
  fulladder fulladder_3 (.ci(fulladder_2_out_5), .a(a2), .b(xor_3_out), .out_4(out_11), .out_5(fulladder_3_out_5));
  fulladder fulladder_4 (.ci(fulladder_3_out_5), .a(a3), .b(xor_4_out), .out_4(out_12), .out_5(out_13));

  // Notes on the sheet:
  //   m
endmodule

module calculadora (
  input  a0,
  input  a1,
  input  a2,
  input  a3,
  input  b0,
  input  b1,
  input  b2,
  input  b3,
  input  in_9,
  input  in_10,
  output out_11,
  output out_12,
  output out_13,
  output out_14
);

  wire multiplicador_c0, multiplicador_c1, multiplicador_c2, multiplicador_c3, somador_p14, somador_p15,
       somador_p16, somador_p17, subtrador_out_9, subtrador_out_10, subtrador_out_11, subtrador_out_12;

  multiplicador multiplicador (
    .a3(a3), .b3(b3), .a2(a2), .b2(b2), .a1(a1), .b1(b1), .a0(a0), .b0(b0), .c3(multiplicador_c3),
    .c2(multiplicador_c2), .c1(multiplicador_c1), .c0(multiplicador_c0));  // open: c7, c6, c5, c4
  // Adder4 somador: pin names not known; wires that end beside it: b0, b1, b2, b3, 1'b0, a0, b0, a1, b1, a2, b2, a3, b3, somador_p14, somador_p15, somador_p16, somador_p17
  subtrador subtrador (
    .a0(a0), .b0(b0), .a1(a1), .b1(b1), .a2(a2), .b2(b2), .a3(a3), .b3(b3), .out_9(subtrador_out_9),
    .out_10(subtrador_out_10), .out_11(subtrador_out_11), .out_12(subtrador_out_12));  // open: out_13
  multiplexador multiplexador_1 (
    .I0(somador_p14), .I1(subtrador_out_9), .I2(multiplicador_c0), .S1(in_9), .S0(in_10), .F(out_11));  // open: I3
  multiplexador multiplexador_2 (
    .I0(somador_p15), .I1(subtrador_out_10), .I2(multiplicador_c1), .S1(in_9), .S0(in_10), .F(out_12));  // open: I3
  multiplexador multiplexador_3 (
    .I0(somador_p16), .I1(subtrador_out_11), .I2(multiplicador_c2), .S1(in_9), .S0(in_10), .F(out_13));  // open: I3
  multiplexador multiplexador_4 (
    .I0(somador_p17), .I1(subtrador_out_12), .I2(multiplicador_c3), .S1(in_9), .S0(in_10), .F(out_14));  // open: I3
endmodule

module multiplexador (
  input  I0,
  input  I1,
  input  I2,
  input  I3,
  input  S1,
  input  S0,
  output F
);

  wire and_1_out, and_2_out, and_3_out, and_4_out;

  and and_1 (and_1_out, I0, ~S1, ~S0);  // AND_Gate
  and and_2 (and_2_out, I1, ~S1, S0);  // AND_Gate
  and and_3 (and_3_out, I2, S1, ~S0);  // AND_Gate
  and and_4 (and_4_out, I3, S1, S0);
  or or_1 (F, and_1_out, and_2_out, and_3_out, and_4_out);
endmodule
